// Logisim project ALU.circ as structural Verilog
module \ALU_1BİT  (
  input  INPR,
  input  DR,
  input  AC,
  input  AND,
  input  Cin,
  input  ADD,
  input  CMA,
  input  LD_DR,
  input  LD_INPR,
  input  CIR,
  input  CIL,
  input  \AC_İ_1 ,
  input  \AC_İ_1_2 ,
  output Cout,
  output AC_OUTPUT
);

  wire ADD_out, adder_1_out, AND_out, CMA_out, LD_DR_out, LD_INPR_out, not_1_out, SHL_out, SHR_out;

  Adder #(.width(1)) adder_1 (.a(AC), .b(DR), .out(adder_1_out), .cin(Cin), .cout(Cout));
  not not_1 (not_1_out, AC);
  and u_AND (AND_out, AND, AC, DR);
  and u_ADD (ADD_out, ADD, adder_1_out);
  and u_CMA (CMA_out, CMA, not_1_out);
  and u_LD_DR (LD_DR_out, LD_DR, DR);
  and u_LD_INPR (LD_INPR_out, LD_INPR, INPR);
  and SHR (SHR_out, CIR, \AC_İ_1_2 );
  and SHL (SHL_out, CIL, \AC_İ_1 );
  or or_1 (AC_OUTPUT, AND_out, ADD_out, CMA_out, LD_DR_out, LD_INPR_out, SHR_out, SHL_out);
endmodule

module \ALU_4BİT  (
  input  Cin,
  input  [3:0] AC,
  input  \E_AC_İ_1__0 ,
  input  [3:0] DR,
  input  [3:0] INPR,
  input  AND,
  input  ADD,
  input  CMA,
  input  LD_DR,
  input  LD_INPR,
  input  CIR,
  input  CIL,
  input  \E_AC_İ_1__3 ,
  output [3:0] AC_OUTPUT,
  output Cout
);

  wire alu_1bi_t_1_cout, alu_1bi_t_2_cout, alu_1bi_t_3_cout;

  \ALU_1BİT  \alu_1bi̇t_1  (
    .AND(AND), .ADD(ADD), .CMA(CMA), .LD_DR(LD_DR), .LD_INPR(LD_INPR), .CIR(CIR), .CIL(CIL),
    .AC_OUTPUT(AC_OUTPUT[0]), .INPR(INPR[0]), .DR(DR[0]), .AC(AC[0]), .Cin(Cin), .\AC_İ_1 (\E_AC_İ_1__0 ),
    .\AC_İ_1_2 (AC[1]), .Cout(alu_1bi_t_1_cout));
  \ALU_1BİT  \alu_1bi̇t_2  (
    .AND(AND), .ADD(ADD), .CMA(CMA), .LD_DR(LD_DR), .LD_INPR(LD_INPR), .CIR(CIR), .CIL(CIL),
    .AC_OUTPUT(AC_OUTPUT[1]), .INPR(INPR[1]), .DR(DR[1]), .AC(AC[1]), .Cin(alu_1bi_t_1_cout),
    .\AC_İ_1 (AC[0]), .\AC_İ_1_2 (AC[2]), .Cout(alu_1bi_t_2_cout));
  \ALU_1BİT  \alu_1bi̇t_3  (
    .AND(AND), .ADD(ADD), .CMA(CMA), .LD_DR(LD_DR), .LD_INPR(LD_INPR), .CIR(CIR), .CIL(CIL),
    .AC_OUTPUT(AC_OUTPUT[2]), .INPR(INPR[2]), .DR(DR[2]), .AC(AC[2]), .Cin(alu_1bi_t_2_cout),
    .\AC_İ_1 (AC[1]), .\AC_İ_1_2 (AC[3]), .Cout(alu_1bi_t_3_cout));
  \ALU_1BİT  \alu_1bi̇t_4  (
    .AND(AND), .ADD(ADD), .CMA(CMA), .LD_DR(LD_DR), .LD_INPR(LD_INPR), .CIR(CIR), .CIL(CIL),
    .AC_OUTPUT(AC_OUTPUT[3]), .INPR(INPR[3]), .DR(DR[3]), .AC(AC[3]), .Cin(alu_1bi_t_3_cout),
    .\AC_İ_1 (AC[2]), .\AC_İ_1_2 (\E_AC_İ_1__3 ), .Cout(Cout));

  // Notes on the sheet:
  //   AC(0)
endmodule

module E (
  input  Cin,
  input  ADD,
  input  \AC_İ_1 ,
  input  CIR,
  input  \AC_İ_1_2 ,
  input  CIL,
  input  CLK,
  output OUTPUT,
  output Cin_2,
  output \AC_İ_1_3 ,
  output \AC_İ_1_4 
);

  wire and_1_out, and_2_out, and_3_out, and_4_out, and_5_out, d_ff_1_q, not_1_out, or_1_out, or_2_out;

  and and_1 (and_1_out, Cin, ADD);
  and and_2 (and_2_out, \AC_İ_1 , CIR);
  or or_1 (or_1_out, and_1_out, and_2_out, and_3_out);
  and and_3 (and_3_out, \AC_İ_1_2 , CIL);
  not not_1 (not_1_out, or_1_out);
  or or_2 (or_2_out, \AC_İ_1 , Cin, \AC_İ_1_2 );
  and and_4 (and_4_out, or_2_out, or_1_out);
  and and_5 (and_5_out, not_1_out, or_2_out);
  S_R_Flip_Flop s_r_ff_1 (.S(and_4_out), .clk(CLK), .R(and_5_out), .Q(OUTPUT));  // open: Qn, preset, reset, en
  D_Flip_Flop d_ff_1 (.clk(CLK), .D(OUTPUT), .Q(d_ff_1_q));  // open: Qn, preset, en, reset
  and and_6 (Cin_2, d_ff_1_q, and_1_out);
  and and_7 (\AC_İ_1_3 , d_ff_1_q, and_2_out);
  and and_8 (\AC_İ_1_4 , d_ff_1_q, and_3_out);
endmodule

module alu_4bit_elde (
  input  [3:0] AC,
  input  [3:0] DR,
  input  [3:0] INPR,
  input  AND,
  input  ADD,
  input  CMA,
  input  LD_DR,
  input  LD_INPR,
  input  CIR,
  input  CIL,
  input  CLK,
  output [3:0] AC_OUTPUT,
  output Cout
);

  wire alu_1bi_t_1_cout, alu_1bi_t_2_cout, alu_1bi_t_3_cout, alu_1bi_t_4_cout, \e_1_ac_i̇_1_3 ,
       \e_1_ac_i̇_1_4 , e_1_cin_2;

  \ALU_1BİT  \alu_1bi̇t_1  (
    .AND(AND), .ADD(ADD), .CMA(CMA), .LD_DR(LD_DR), .LD_INPR(LD_INPR), .CIR(CIR), .CIL(CIL),
    .AC_OUTPUT(AC_OUTPUT[0]), .INPR(INPR[0]), .DR(DR[0]), .AC(AC[0]), .Cin(e_1_cin_2),
    .\AC_İ_1 (\e_1_ac_i̇_1_3 ), .\AC_İ_1_2 (AC[1]), .Cout(alu_1bi_t_1_cout));
  \ALU_1BİT  \alu_1bi̇t_2  (
    .AND(AND), .ADD(ADD), .CMA(CMA), .LD_DR(LD_DR), .LD_INPR(LD_INPR), .CIR(CIR), .CIL(CIL),
    .AC_OUTPUT(AC_OUTPUT[1]), .INPR(INPR[1]), .DR(DR[1]), .AC(AC[1]), .Cin(alu_1bi_t_1_cout),
    .\AC_İ_1 (AC[0]), .\AC_İ_1_2 (AC[2]), .Cout(alu_1bi_t_2_cout));
  \ALU_1BİT  \alu_1bi̇t_3  (
    .AND(AND), .ADD(ADD), .CMA(CMA), .LD_DR(LD_DR), .LD_INPR(LD_INPR), .CIR(CIR), .CIL(CIL),
    .AC_OUTPUT(AC_OUTPUT[2]), .INPR(INPR[2]), .DR(DR[2]), .AC(AC[2]), .Cin(alu_1bi_t_2_cout),
    .\AC_İ_1 (AC[1]), .\AC_İ_1_2 (AC[3]), .Cout(alu_1bi_t_3_cout));
  \ALU_1BİT  \alu_1bi̇t_4  (
    .AND(AND), .ADD(ADD), .CMA(CMA), .LD_DR(LD_DR), .LD_INPR(LD_INPR), .CIR(CIR), .CIL(CIL),
    .AC_OUTPUT(AC_OUTPUT[3]), .INPR(INPR[3]), .DR(DR[3]), .AC(AC[3]), .Cin(alu_1bi_t_3_cout),
    .\AC_İ_1 (AC[2]), .\AC_İ_1_2 (\e_1_ac_i̇_1_4 ), .Cout(alu_1bi_t_4_cout));
  E e_1 (
    .Cin(alu_1bi_t_4_cout), .ADD(ADD), .\AC_İ_1 (\e_1_ac_i̇_1_4 ), .CIR(CIR), .\AC_İ_1_2 (\e_1_ac_i̇_1_3 ),
    .CIL(CIL), .CLK(CLK), .OUTPUT(Cout), .Cin_2(e_1_cin_2), .\AC_İ_1_3 (\e_1_ac_i̇_1_3 ),
    .\AC_İ_1_4 (\e_1_ac_i̇_1_4 ));

  // Notes on the sheet:
  //   AC(0)
endmodule
