// Logisim project PROJEM.circ as structural Verilog: 3 circuits, main circuit register_kontrol
module main (
  input  [3:0] in_1,
  output out_2
);

  wire clock_1_out, main_kontrol_1_dr_load, main_kontrol_1_hlt, main_kontrol_1_outr, not_1_out;
  wire [1:0] main_kontrol_1_ir_bus_ir_load, main_kontrol_1_m____bus_m____load;
  wire [2:0] main_kontrol_1_ar_bus_ar_inc_ar_load, main_kontrol_1_pc_bus_pc_inc_pc_load;
  wire [3:0] AC_output, alu_4bit_elde_1_ac_output, AR_output, controlled_buffer_1_out,
       controlled_buffer_1_out_2, DR_output, INPR_output, IR_ir_0_3, IR_ir_4_7,
       main_kontrol_1_ac_bus_ac_clear_ac_inc_ac_load, OUTR_output, PC_output;
  wire [6:0] main_kontrol_1_alu;
  wire [7:0] ram_1_data;

  Clock clock_1 (.out(clock_1_out));
  main_kontrol main_kontrol_1 (
    .IR_4_7(IR_ir_4_7), .CLOCK(main_kontrol_1_ac_bus_ac_clear_ac_inc_ac_load[0]),
    .M____BUS_M____LOAD(main_kontrol_1_m____bus_m____load),
    .AR_BUS_AR_INC_AR_LOAD(main_kontrol_1_ar_bus_ar_inc_ar_load),
    .PC_BUS_PC_INC_PC_LOAD(main_kontrol_1_pc_bus_pc_inc_pc_load), .DR_LOAD(main_kontrol_1_dr_load),
    .AC_BUS_AC_CLEAR_AC_INC_AC_LOAD(main_kontrol_1_ac_bus_ac_clear_ac_inc_ac_load),
    .OUTR(main_kontrol_1_outr), .IR_BUS_IR_LOAD(main_kontrol_1_ir_bus_ir_load), .ALU(main_kontrol_1_alu),
    .HLT(main_kontrol_1_hlt));  // open: E_BUS_E_CLEAR_E_LOAD
  not not_1 (not_1_out, main_kontrol_1_hlt);
  and and_1 (main_kontrol_1_ac_bus_ac_clear_ac_inc_ac_load[0], not_1_out, clock_1_out);
  // Probe on INPR_output
  _4_Bitlik_Register INPR (
    .\İnput (in_1), .CLK(main_kontrol_1_ac_bus_ac_clear_ac_inc_ac_load[0]), .\output (INPR_output));  // open: INC, LD, CLR
  alu_4bit_elde alu_4bit_elde_1 (
    .AC(AC_output), .DR(DR_output), .INPR(INPR_output), .AND(main_kontrol_1_alu[0]),
    .ADD(main_kontrol_1_alu[1]), .CMA(main_kontrol_1_alu[2]), .LD_DR(main_kontrol_1_alu[3]),
    .LD_INPR(main_kontrol_1_alu[4]), .CIR(main_kontrol_1_alu[5]), .CIL(main_kontrol_1_alu[6]), .Cout(out_2),
    .CLK(main_kontrol_1_ac_bus_ac_clear_ac_inc_ac_load[0]), .AC_OUTPUT(alu_4bit_elde_1_ac_output));
  RAM #(.addrWidth(4), .bus("separate")) ram_1 (
    .addr(AR_output), .din({controlled_buffer_1_out_2, controlled_buffer_1_out}), .data(ram_1_data),
    .str(main_kontrol_1_m____bus_m____load[0]), .clk(main_kontrol_1_ac_bus_ac_clear_ac_inc_ac_load[0]));  // open: sel, ld, clr
  // Probe on AR_output
  _4_Bitlik_Register AR (
    .\İnput (controlled_buffer_1_out), .CLK(main_kontrol_1_ac_bus_ac_clear_ac_inc_ac_load[0]),
    .INC(main_kontrol_1_ar_bus_ar_inc_ar_load[1]), .LD(main_kontrol_1_ar_bus_ar_inc_ar_load[0]),
    .\output (AR_output));  // open: CLR
  _4_Bitlik_Register PC (
    .\İnput (controlled_buffer_1_out), .CLK(main_kontrol_1_ac_bus_ac_clear_ac_inc_ac_load[0]),
    .INC(main_kontrol_1_pc_bus_pc_inc_pc_load[1]), .LD(main_kontrol_1_pc_bus_pc_inc_pc_load[0]),
    .\output (PC_output));  // open: CLR
  _4_Bitlik_Register DR (
    .\İnput (controlled_buffer_1_out), .CLK(main_kontrol_1_ac_bus_ac_clear_ac_inc_ac_load[0]),
    .LD(main_kontrol_1_dr_load), .\output (DR_output));  // open: INC, CLR
  // Probe on DR_output
  // Probe on AC_output
  _4_Bitlik_Register AC (
    .\İnput (alu_4bit_elde_1_ac_output), .CLK(main_kontrol_1_ac_bus_ac_clear_ac_inc_ac_load[0]),
    .INC(main_kontrol_1_ac_bus_ac_clear_ac_inc_ac_load[1]),
    .LD(main_kontrol_1_ac_bus_ac_clear_ac_inc_ac_load[0]),
    .CLR(main_kontrol_1_ac_bus_ac_clear_ac_inc_ac_load[2]), .\output (AC_output));
  _4_Bitlik_Register OUTR (
    .\İnput (controlled_buffer_1_out), .CLK(main_kontrol_1_ac_bus_ac_clear_ac_inc_ac_load[0]),
    .LD(main_kontrol_1_outr), .\output (OUTR_output));  // open: INC, CLR
  // Probe on OUTR_output
  // Probe on IR_ir_0_3
  // Probe on IR_ir_4_7
  IR IR (
    .\İNPUT ({controlled_buffer_1_out_2, controlled_buffer_1_out}),
    .CLK(main_kontrol_1_ac_bus_ac_clear_ac_inc_ac_load[0]), .LD(main_kontrol_1_ir_bus_ir_load[0]),
    .IR_0_3(IR_ir_0_3), .IR_4_7(IR_ir_4_7));
  assign {controlled_buffer_1_out_2, controlled_buffer_1_out} = main_kontrol_1_ar_bus_ar_inc_ar_load[2] ? {4'b0000, AR_output} : 8'bz;  // Controlled_Buffer controlled_buffer_1
  assign {controlled_buffer_1_out_2, controlled_buffer_1_out} = main_kontrol_1_pc_bus_pc_inc_pc_load[2] ? {4'b0000, PC_output} : 8'bz;  // Controlled_Buffer controlled_buffer_2
  assign {controlled_buffer_1_out_2, controlled_buffer_1_out} = main_kontrol_1_ac_bus_ac_clear_ac_inc_ac_load[3] ? {4'b0000, AC_output} : 8'bz;  // Controlled_Buffer controlled_buffer_3
  assign {controlled_buffer_1_out_2, controlled_buffer_1_out} = main_kontrol_1_ir_bus_ir_load[1] ? {4'b0000, IR_ir_0_3} : 8'bz;  // Controlled_Buffer controlled_buffer_4
  assign {controlled_buffer_1_out_2, controlled_buffer_1_out} = main_kontrol_1_m____bus_m____load[1] ? ram_1_data : 8'bz;  // Controlled_Buffer controlled_buffer_5
  // Probe on PC_output

  // Notes on the sheet:
  //   IR(4-7)
  //   ALU
endmodule

// main kontrol
module main_kontrol (
  input  [3:0] IR_4_7,
  input  CLOCK,
  output [1:0] M____BUS_M____LOAD,
  output [2:0] AR_BUS_AR_INC_AR_LOAD,
  output [2:0] PC_BUS_PC_INC_PC_LOAD,
  output DR_LOAD,
  output [3:0] AC_BUS_AC_CLEAR_AC_INC_AC_LOAD,
  output OUTR,
  output [1:0] IR_BUS_IR_LOAD,
  output [2:0] E_BUS_E_CLEAR_E_LOAD,
  output [6:0] ALU,
  output HLT
);

  wire decoder_1_out15, main_1_sc_clear;
  wire [1:0] decoder_2_out4;
  wire [2:0] decoder_2_out0;
  wire [3:0] main_2_output;
  wire [6:0] decoder_1_out0;
  wire [14:3] decoder_1_out3;

  SC_CLEAR_main main_1 (
    .T3(decoder_2_out4[1]), .T4(decoder_2_out4[0]), .D0(decoder_1_out0[0]), .D1(decoder_1_out0[1]),
    .D2(decoder_1_out0[2]), .D3(decoder_1_out3[3]), .D4(decoder_1_out3[4]), .D5(decoder_1_out3[5]),
    .D6(decoder_1_out3[6]), .D7(decoder_1_out3[7]), .D8(decoder_1_out3[8]), .D9(decoder_1_out0[3]),
    .D10(decoder_1_out3[10]), .D11(decoder_1_out0[4]), .D12(decoder_1_out0[5]), .D13(decoder_1_out0[6]),
    .D14(decoder_1_out3[14]), .SC_CLEAR(main_1_sc_clear));
  Decoder #(.select(4)) decoder_1 (
    .out0(decoder_1_out0[0]), .out1(decoder_1_out0[1]), .out2(decoder_1_out0[2]), .out3(decoder_1_out3[3]),
    .out4(decoder_1_out3[4]), .out5(decoder_1_out3[5]), .out6(decoder_1_out3[6]), .out7(decoder_1_out3[7]),
    .out8(decoder_1_out3[8]), .out9(decoder_1_out0[3]), .out10(decoder_1_out3[10]),
    .out11(decoder_1_out0[4]), .out12(decoder_1_out0[5]), .out13(decoder_1_out0[6]),
    .out14(decoder_1_out3[14]), .out15(decoder_1_out15), .sel(IR_4_7));  // open: en
  Decoder #(.select(4)) decoder_2 (
    .out0(decoder_2_out0[0]), .out1(decoder_2_out0[1]), .out2(decoder_2_out0[2]), .out3(decoder_2_out4[1]),
    .out4(decoder_2_out4[0]), .sel(main_2_output));  // open: out5, out6, out7, out8, out9, out10, out11, out12, out13, out14, out15, en
  counter_main main_2 (.CLOCK(CLOCK), .SC_CLEAR(main_1_sc_clear), .OUTPUT(main_2_output));
  and and_1 (HLT, decoder_2_out4[1], decoder_1_out15);
  ALU alu_1 (
    .T3(decoder_2_out4[1]), .T4(decoder_2_out4[0]), .D0(decoder_1_out0[0]), .D1(decoder_1_out0[1]),
    .D2(decoder_1_out0[2]), .D9(decoder_1_out0[3]), .D11(decoder_1_out0[4]), .D12(decoder_1_out0[5]),
    .D13(decoder_1_out0[6]), .AND(ALU[0]), .ADD(ALU[1]), .CMA(ALU[2]), .DR_LOAD(ALU[3]), .LD_INPR(ALU[4]),
    .CIR(ALU[5]), .CIL(ALU[6]));
  register_kontrol register_kontrol_1 (
    .T0(decoder_2_out0[0]), .T1(decoder_2_out0[1]), .T2(decoder_2_out0[2]), .T3(decoder_2_out4[1]),
    .T4(decoder_2_out4[0]), .D0(decoder_1_out0[0]), .D1(decoder_1_out0[1]), .D2(decoder_1_out0[2]),
    .D3(decoder_1_out3[3]), .D4(decoder_1_out3[4]), .D5(decoder_1_out3[5]), .D6(decoder_1_out3[6]),
    .D7(decoder_1_out3[7]), .D8(decoder_1_out3[8]), .D9(decoder_1_out0[3]), .D10(decoder_1_out3[10]),
    .D11(decoder_1_out0[4]), .D12(decoder_1_out0[5]), .D13(decoder_1_out0[6]), .D14(decoder_1_out3[14]),
    .M___BUS_M___LOAD(M____BUS_M____LOAD), .AR_BUS_AR_INC_AR_LOAD(AR_BUS_AR_INC_AR_LOAD),
    .PC_BUS_PC_INC_PC_LOAD(PC_BUS_PC_INC_PC_LOAD), .DR_LOAD(DR_LOAD),
    .AC_BUS_AC_CLEAR_AC_INC_AC_LOAD(AC_BUS_AC_CLEAR_AC_INC_AC_LOAD), .OUTR_LOAD(OUTR),
    .IR_BUS_IR_LOAD(IR_BUS_IR_LOAD), .E_BUS_E_CLEAR_E_LOAD(E_BUS_E_CLEAR_E_LOAD));

  // Notes on the sheet:
  //   T(3-4)
  //   D(0-14)
  //   SC_CLEAR
  //   D(0-15)
  //   T(0-4)
  //   counter
  //   ALU_KONTROL
  //   T(0-4)
  //   D(0-14)
  //   REGİSTER KONTROL
endmodule

module register_kontrol (
  input  T0,
  input  T1,
  input  T2,
  input  T3,
  input  T4,
  input  D0,
  input  D1,
  input  D2,
  input  D3,
  input  D4,
  input  D5,
  input  D6,
  input  D7,
  input  D8,
  input  D9,
  input  D10,
  input  D11,
  input  D12,
  input  D13,
  input  D14,
  output [1:0] M___BUS_M___LOAD,
  output [2:0] AR_BUS_AR_INC_AR_LOAD,
  output [2:0] PC_BUS_PC_INC_PC_LOAD,
  output DR_LOAD,
  output [3:0] AC_BUS_AC_CLEAR_AC_INC_AC_LOAD,
  output OUTR_LOAD,
  output [1:0] IR_BUS_IR_LOAD,
  output [2:0] E_BUS_E_CLEAR_E_LOAD
);

  OUTR OUTR (.T3(T3), .D14(D14), .OUTR_LOAD(OUTR_LOAD));
  IR IR (.T1(T1), .T2(T2), .IR_LOAD(IR_BUS_IR_LOAD[0]), .IR_BUS(IR_BUS_IR_LOAD[1]));
  M M (
    .M____BUS(M___BUS_M___LOAD[1]), .T1(T1), .T3(T3), .D0(D0), .D1(D1), .D2(D2), .D3(D3), .D5(D5), .D6(D6),
    .M____LOAD(M___BUS_M___LOAD[0]));
  AR AR (
    .T0(T0), .T2(T2), .T3(T3), .T4(T4), .D4(D4), .D5(D5), .AR_LOAD(AR_BUS_AR_INC_AR_LOAD[0]),
    .AR_INC(AR_BUS_AR_INC_AR_LOAD[1]), .AR_BUS(AR_BUS_AR_INC_AR_LOAD[2]));
  PC PC (
    .T0(T0), .T1(T1), .T3(T3), .T4(T4), .D4(D4), .D5(D5), .D6(D6), .PC_LOAD(PC_BUS_PC_INC_PC_LOAD[0]),
    .PC_INC(PC_BUS_PC_INC_PC_LOAD[1]), .PC_BUS(PC_BUS_PC_INC_PC_LOAD[2]));
  DR DR (.T3(T3), .D0(D0), .D1(D1), .D2(D2), .DR_LOAD(DR_LOAD));
  E E (
    .T3(T3), .T4(T4), .D1(D1), .D8(D8), .D11(D11), .D12(D12), .E_LOAD(E_BUS_E_CLEAR_E_LOAD[0]),
    .E_CLEAR(E_BUS_E_CLEAR_E_LOAD[1]), .E_BUS(E_BUS_E_CLEAR_E_LOAD[2]));
  AC AC (
    .T3(T3), .T4(T4), .D0(D0), .D1(D1), .D2(D2), .D3(D3), .D7(D7), .D9(D9), .D10(D10), .D11(D11), .D12(D12),
    .D13(D13), .D14(D14), .AC_LOAD(AC_BUS_AC_CLEAR_AC_INC_AC_LOAD[0]),
    .AC_INC(AC_BUS_AC_CLEAR_AC_INC_AC_LOAD[1]), .AC_CLEAR(AC_BUS_AC_CLEAR_AC_INC_AC_LOAD[2]),
    .AC_BUS(AC_BUS_AC_CLEAR_AC_INC_AC_LOAD[3]));
endmodule
