// Logisim project SC_CLEAR.circ as structural Verilog: 1 circuit, main circuit main
module main (
  input  T3,
  input  T4,
  input  D0,
  input  D1,
  input  D2,
  input  D3,
  input  D4,
  input  D5,
  input  D6,
  input  D7,
  input  D8,
  input  D9,
  input  D10,
  input  D11,
  input  D12,
  input  D13,
  input  D14,
  output SC_CLEAR
);

  wire and_1_out, and_2_out, or_1_out, or_2_out;

  or or_1 (or_1_out, D0, D1, D2, D5);
  or or_2 (or_2_out, D14, D13, D12, D11, D10, D9, D8, D7, D6, D4, D3);
  and and_1 (and_1_out, or_2_out, T3);
  and and_2 (and_2_out, or_1_out, T4);
  or or_3 (SC_CLEAR, and_1_out, and_2_out);
endmodule
