// Logisim project counter.circ as structural Verilog: 1 circuit, main circuit main
module main (
  input  CLOCK,
  input  SC_CLEAR,
  output [3:0] OUTPUT
);

  wire and_1_out, register_1_q;

  Counter #(.width(4), .max('hf)) counter_1 (
    .count(1'b1), .Q(OUTPUT), .clk(CLOCK), .clr(register_1_q));  // open: load, D, carry
  Register #(.width(1)) register_1 (.D(SC_CLEAR), .Q(register_1_q), .clk(CLOCK), .clr(and_1_out));  // open: en
  and and_1 (and_1_out, CLOCK, SC_CLEAR);
endmodule
