// Logisim project kontrol_üniteleri.circ as structural Verilog
module AR (
  input  T0,
  input  T2,
  input  T3,
  input  T4,
  input  D4,
  input  D5,
  output AR_LOAD,
  output AR_INC,
  output AR_BUS
);

  wire and_2_out, and_3_out;

  or or_1 (AR_LOAD, T0, T2);
  and and_1 (AR_INC, D5, T3);
  and and_2 (and_2_out, D4, T3);
  or or_2 (AR_BUS, and_2_out, and_3_out);
  and and_3 (and_3_out, D5, T4);
endmodule

module PC (
  input  T0,
  input  T1,
  input  T3,
  input  T4,
  input  D4,
  input  D5,
  input  D6,
  output PC_LOAD,
  output PC_INC,
  output PC_BUS
);

  wire and_1_out, and_2_out, and_3_out, or_1_out;

  or or_1 (or_1_out, D4, D6);
  and and_1 (and_1_out, or_1_out, T3);
  and and_2 (and_2_out, D4, D5);
  and and_3 (and_3_out, T3, D5);
  or or_2 (PC_LOAD, and_1_out, and_2_out);
  or or_3 (PC_BUS, and_3_out, T0);

  assign PC_INC = T1;
endmodule

module M (
  input  T1,
  input  T3,
  input  D0,
  input  D1,
  input  D2,
  input  D3,
  input  D5,
  input  D6,
  output M____LOAD,
  output M____BUS
);

  wire and_1_out, or_1_out, or_2_out;

  or or_1 (or_1_out, D5, D3);
  or or_2 (or_2_out, D0, D1, D2, D6);
  and and_1 (and_1_out, or_2_out, T3);
  and and_2 (M____LOAD, or_1_out, T3);
  or or_3 (M____BUS, and_1_out, T1);
endmodule

module DR (
  input  T3,
  input  D0,
  input  D1,
  input  D2,
  output DR_LOAD
);

  wire or_1_out;

  or or_1 (or_1_out, D2, D1, D0);
  and and_1 (DR_LOAD, or_1_out, T3);
endmodule

module OUTR (
  input  T3,
  input  D14,
  output OUTR_LOAD
);

  and and_1 (OUTR_LOAD, D14, T3);
endmodule

module IR (
  input  T1,
  input  T2,
  output IR_LOAD,
  output IR_BUS
);


  assign IR_BUS = T2;
  assign IR_LOAD = T1;
endmodule

module E (
  input  T3,
  input  T4,
  input  D1,
  input  D8,
  input  D11,
  input  D12,
  output E_LOAD,
  output E_CLEAR,
  output E_BUS
);

  wire and_1_out, and_2_out, or_1_out, or_2_out;

  or or_1 (or_1_out, D12, D11);
  and and_1 (and_1_out, D1, T4);
  and and_2 (and_2_out, or_1_out, T3);
  or or_2 (or_2_out, D12, D11);
  or or_3 (E_LOAD, and_1_out, and_2_out);
  and and_3 (E_CLEAR, D8, T3);
  and and_4 (E_BUS, or_2_out, T3);
endmodule

module AC (
  input  T3,
  input  T4,
  input  D0,
  input  D1,
  input  D2,
  input  D3,
  input  D7,
  input  D9,
  input  D10,
  input  D11,
  input  D12,
  input  D13,
  input  D14,
  output AC_LOAD,
  output AC_INC,
  output AC_CLEAR,
  output AC_BUS
);

  wire and_1_out, and_2_out, or_1_out, or_2_out, or_3_out;

  or or_1 (or_1_out, D0, D2, D1);
  or or_2 (or_2_out, D9, D11, D12, D13);
  or or_3 (or_3_out, D14, D3);
  and and_1 (and_1_out, or_1_out, T4);
  and and_2 (and_2_out, T3, or_2_out);
  or or_4 (AC_LOAD, and_1_out, and_2_out);
  and and_3 (AC_INC, T3, D10);
  and and_4 (AC_CLEAR, D7, T3);
  and and_5 (AC_BUS, or_3_out, T3);
endmodule

module ALU (
  input  T3,
  input  T4,
  input  D0,
  input  D1,
  input  D2,
  input  D9,
  input  D11,
  input  D12,
  input  D13,
  output AND,
  output ADD,
  output CMA,
  output DR_LOAD,
  output LD_INPR,
  output CIR,
  output CIL
);

  and and_1 (AND, D0, T4);
  and and_2 (ADD, D1, T4);
  and and_3 (CMA, D9, T3);
  and and_4 (DR_LOAD, D2, T4);
  and and_5 (LD_INPR, D13, T3);
  and and_6 (CIR, D11, T3);
  and and_7 (CIL, D12, T3);
endmodule
