// Logisim project register.circ as structural Verilog: 3 circuits, main circuit main
module main (
  input  [3:0] \İNPUT ,
  input  CLK,
  input  LD,
  input  INC,
  input  CLR,
  output [3:0] OUTPUT
);

  _4_Bitlik_Register u_4_bitlik_register_1 (
    .\İnput (\İNPUT ), .CLK(CLK), .INC(LD), .LD(INC), .CLR(CLR), .\output (OUTPUT));
endmodule

// reg
module _4_Bitlik_Register (
  input  INC,
  input  LD,
  input  [3:0] \İnput ,
  input  CLK,
  input  CLR,
  output [3:0] \output 
);

  wire and_1_out, and_2_out, and_3_out, and_4_out, and_5_out, and_6_out, and_7_out, and_8_out, and_9_out,
       and_10_out, and_11_out, and_12_out, not_1_out, not_2_out, not_3_out, not_4_out, not_5_out, not_6_out,
       or_1_out, or_2_out, or_3_out, or_4_out, or_5_out, or_6_out, or_7_out, or_8_out;

  not not_1 (not_1_out, LD);
  and and_1 (and_1_out, INC, not_1_out);
  not not_2 (not_2_out, not_1_out);
  not not_3 (not_3_out, \İnput [0]);
  not not_4 (not_4_out, \İnput [1]);
  not not_5 (not_5_out, \İnput [2]);
  not not_6 (not_6_out, \İnput [3]);
  and and_2 (and_2_out, not_2_out, \İnput [0]);
  and and_3 (and_3_out, not_2_out, not_3_out);
  and and_4 (and_4_out, not_2_out, \İnput [1]);
  and and_5 (and_5_out, not_2_out, not_4_out);
  and and_6 (and_6_out, not_2_out, \İnput [2]);
  and and_7 (and_7_out, not_2_out, not_5_out);
  and and_8 (and_8_out, not_2_out, \İnput [3]);
  and and_9 (and_9_out, not_2_out, not_6_out);
  and and_10 (and_10_out, and_1_out, \output [0]);
  and and_11 (and_11_out, and_1_out, \output [0], \output [1]);
  and and_12 (and_12_out, \output [2], \output [1], \output [0], and_1_out);
  or or_1 (or_1_out, and_2_out, and_1_out);
  or or_2 (or_2_out, and_3_out, and_1_out);
  or or_3 (or_3_out, and_4_out, and_10_out);
  or or_4 (or_4_out, and_10_out, and_5_out);
  or or_5 (or_5_out, and_6_out, and_11_out);
  or or_6 (or_6_out, and_11_out, and_7_out);
  or or_7 (or_7_out, and_8_out, and_12_out);
  or or_8 (or_8_out, and_12_out, and_9_out);
  J_K_Flip_Flop j_k_ff_1 (.J(or_1_out), .clk(CLK), .K(or_2_out), .Q(\output [0]), .reset(CLR));  // open: Qn, preset, en
  J_K_Flip_Flop j_k_ff_2 (.J(or_3_out), .clk(CLK), .K(or_4_out), .Q(\output [1]), .reset(CLR));  // open: Qn, preset, en
  J_K_Flip_Flop j_k_ff_3 (.J(or_5_out), .clk(CLK), .K(or_6_out), .Q(\output [2]), .reset(CLR));  // open: Qn, preset, en
  J_K_Flip_Flop j_k_ff_4 (.J(or_7_out), .clk(CLK), .K(or_8_out), .Q(\output [3]), .reset(CLR));  // open: Qn, preset, en
endmodule

module IR (
  input  [7:0] \İNPUT ,
  input  CLK,
  input  LD,
  output [3:0] IR_0_3,
  output [3:0] IR_4_7
);

  _4_Bitlik_Register u_4_bitlik_register_1 (
    .\İnput (\İNPUT [3:0]), .CLK(CLK), .LD(LD), .\output (IR_0_3));  // open: INC, CLR
  _4_Bitlik_Register u_4_bitlik_register_2 (
    .\İnput (\İNPUT [7:4]), .CLK(CLK), .LD(LD), .\output (IR_4_7));  // open: INC, CLR
endmodule
